// Logisim project assignment3.circ as structural Verilog
module p1_rs_latch_gate (
  input  R,
  input  S,
  output Q,
  output Qn
);

  nor nor_1 (Q, R, Qn);
  nor nor_2 (Qn, Q, S);
endmodule

module p1_rs_latch_vhdl (
  input  s,
  input  r,
  output q,
  output qn
);

  rs_latch rs_latch_1 (.s(s), .r(r), .q(q), .qn(qn));
endmodule

module p2_d_latch_gate (
  input  D,
  input  en,
  output Q,
  output Qn
);

  wire nand_1_out, nand_2_out, not_1_out;

  nand nand_1 (nand_1_out, D, en);
  not not_1 (not_1_out, D);
  nand nand_2 (nand_2_out, not_1_out, en);
  nand nand_3 (Q, nand_1_out, Qn);
  nand nand_4 (Qn, Q, nand_2_out);
endmodule

module p2_d_latch_vhdl (
  input  d,
  input  en,
  output q,
  output qn
);

  d_latch d_latch_1 (.d(d), .en(en), .q(q), .qn(qn));
endmodule

module p3_d_ff_gate (
  input  D,
  input  clk,
  output Q,
  output Qn
);

  wire G1_out, G2_out, G3_out, G4_out, G5_out, G6_out, not_1_out, not_2_out, not_3_out, not_4_out;

  not not_1 (not_1_out, clk);
  not not_2 (not_2_out, D);
  nand G1 (G1_out, D, not_1_out);
  nand G2 (G2_out, not_2_out, not_1_out);
  nand G3 (G3_out, G1_out, G4_out);
  nand G4 (G4_out, G3_out, G2_out);
  not not_3 (not_3_out, not_1_out);
  not not_4 (not_4_out, G3_out);
  nand G5 (G5_out, G3_out, not_3_out);
  nand G6 (G6_out, not_4_out, not_3_out);
  nand G7 (Q, G5_out, Qn);
  nand G8 (Qn, Q, G6_out);
endmodule

module p3_d_ff_vhdl (
  input  d,
  input  clk,
  output q,
  output qn
);

  d_ff d_ff_1 (.d(d), .clk(clk), .q(q), .qn(qn));
endmodule

module p4_jk_ff_gate (
  input  J,
  input  K,
  input  clk,
  input  CLR,
  output Q,
  output Qn
);

  wire G1_out, G2_out, G3_out, G4_out, G5_out, G6_out, not_1_out, not_2_out;

  not not_1 (not_1_out, clk);
  nand G1 (G1_out, J, Qn, not_1_out);
  nand G2 (G2_out, not_1_out, Q, K);
  not not_2 (not_2_out, not_1_out);
  nand G3 (G3_out, G1_out, G4_out);
  nand G4 (G4_out, G3_out, CLR, G2_out);
  nand G5 (G5_out, G3_out, not_2_out);
  nand G6 (G6_out, not_2_out, G4_out);
  nand G7 (Q, G5_out, Qn);
  nand G8 (Qn, Q, CLR, G6_out);
endmodule

module p4_jk_ff_vhdl (
  input  j,
  input  k,
  input  clk,
  output q,
  output qn
);

  jk_ff jk_ff_1 (.j(j), .k(k), .clk(clk), .q(q), .qn(qn));
endmodule

module p5_d_ff_sc_gate (
  input  set,
  input  D,
  input  clk,
  input  clr,
  output Q,
  output Qn
);

  wire G1_out, G2_out, G3_out, G4_out, G5_out, G6_out, G9_out, not_1_out, not_2_out, not_3_out, not_4_out,
       not_5_out;

  not not_1 (not_1_out, clk);
  nand G9 (G9_out, set, not_3_out);
  not not_2 (not_2_out, D);
  not not_3 (not_3_out, clr);
  nand G1 (G1_out, D, not_1_out);
  nand G2 (G2_out, not_2_out, not_1_out);
  nand G3 (G3_out, G1_out, G9_out, G4_out);
  nand G4 (G4_out, G3_out, not_3_out, G2_out);
  not not_4 (not_4_out, not_1_out);
  not not_5 (not_5_out, G3_out);
  nand G5 (G5_out, G3_out, not_4_out);
  nand G6 (G6_out, not_5_out, not_4_out);
  nand G7 (Q, G5_out, G9_out, Qn);
  nand G8 (Qn, Q, not_3_out, G6_out);
endmodule

module p5_d_ff_sc_vhdl (
  input  in_1,
  input  in_2,
  input  in_3,
  input  in_4,
  output q,
  output qn
);

  d_ff_sc d_ff_sc_1 (.d(in_1), .clk(in_2), .set(in_3), .clr(in_4), .q(q), .qn(qn));
endmodule

// VHDL entity rs_latch, as the project stores it:
library ieee;
use ieee.std_logic_1164.all;

-- RS latch : two cross-coupled NOR gates
entity rs_latch is
    port(
        s, r  : in  std_logic;
        q, qn : out std_logic
    );
end entity rs_latch;

architecture bhv of rs_latch is
    signal q_i  : std_logic := '0';
    signal qn_i : std_logic := '1';
begin
    q_i  <= r nor qn_i;   -- upper NOR : Q  = (R + Q')'
    qn_i <= s nor q_i;    -- lower NOR : Q' = (S + Q)'

    q  <= q_i;
    qn <= qn_i;
end architecture bhv;

// VHDL entity d_latch, as the project stores it:
library ieee;
use ieee.std_logic_1164.all;

-- D latch with enable (level triggered)
entity d_latch is
    port(
        d, en : in  std_logic;
        q, qn : out std_logic
    );
end entity d_latch;

architecture bhv of d_latch is
    signal q_i : std_logic := '0';
begin
    process(d, en)
    begin
        if en = '1' then
            q_i <= d;        -- en=1 : transparent, Q follows D
        end if;              -- en=0 : no assignment -> keeps old value
    end process;

    q  <= q_i;
    qn <= not q_i;
end architecture bhv;

// VHDL entity d_ff, as the project stores it:
library ieee;
use ieee.std_logic_1164.all;

-- Positive-edge-triggered D flip-flop
entity d_ff is
    port(
        d, clk : in  std_logic;
        q, qn  : out std_logic
    );
end entity d_ff;

architecture bhv of d_ff is
    signal q_i : std_logic := '0';
begin
    process(clk)
    begin
        if rising_edge(clk) then   -- only at the 0 -> 1 moment of clk
            q_i <= d;
        end if;
    end process;

    q  <= q_i;
    qn <= not q_i;
end architecture bhv;

// VHDL entity jk_ff, as the project stores it:
library ieee;
use ieee.std_logic_1164.all;

-- Positive-edge-triggered JK flip-flop
--   JK = 00 Hold, 01 Reset, 10 Set, 11 Toggle
entity jk_ff is
    port(
        j, k, clk : in  std_logic;
        q, qn     : out std_logic
    );
end entity jk_ff;

architecture bhv of jk_ff is
    signal q_i : std_logic := '0';
    signal jk  : std_logic_vector(1 downto 0);
begin
    jk <= j & k;               -- combine J and K into 2 bits

    process(clk)
    begin
        if rising_edge(clk) then
            case jk is
                when "00"   => q_i <= q_i;       -- Hold
                when "01"   => q_i <= '0';       -- Reset
                when "10"   => q_i <= '1';       -- Set
                when "11"   => q_i <= not q_i;   -- Toggle
                when others => q_i <= q_i;
            end case;
        end if;
    end process;

    q  <= q_i;
    qn <= not q_i;
end architecture bhv;

// VHDL entity d_ff_sc, as the project stores it:
library ieee;
use ieee.std_logic_1164.all;

-- Positive-edge D flip-flop with asynchronous set / clear
--   clr = '1'             : Q <= '0' immediately (highest priority)
--   set = '1' (clr = '0') : Q <= '1' immediately
--   otherwise             : normal D flip-flop
entity d_ff_sc is
    port(
        d, clk   : in  std_logic;
        set, clr : in  std_logic;
        q, qn    : out std_logic
    );
end entity d_ff_sc;

architecture bhv of d_ff_sc is
    signal q_i : std_logic := '0';
begin
    process(clk, set, clr)
    begin
        if clr = '1' then              -- checked first -> clear has priority
            q_i <= '0';
        elsif set = '1' then
            q_i <= '1';
        elsif rising_edge(clk) then
            q_i <= d;
        end if;
    end process;

    q  <= q_i;
    qn <= not q_i;
end architecture bhv;
